# Fritzing sketch lra (saved by Fritzing 0.9.6b)
breadboards: 1

parts:
  A1 = Arduino R4 Minima
  Bauteil13 = GY-VL53L0XV2 Laser Ranger Module
  Bauteil11 = GY-VL53L0XV2 Laser Ranger Module
  Bauteil10 = GY-VL53L0XV2 Laser Ranger Module
  Bauteil9 = GY-VL53L0XV2 Laser Ranger Module
  Bauteil12 = GY-VL53L0XV2 Laser Ranger Module

nets:
  VCC: A1.Pin_5, Bauteil13.VCC, Bauteil11.VCC, Bauteil10.VCC, Bauteil9.VCC, Bauteil12.VCC
  GND: A1.Pin_6, Bauteil13.GND, Bauteil11.GND, Bauteil10.GND, Bauteil9.GND, Bauteil12.GND
  N1: A1.Pin_13, Bauteil13.SDA, Bauteil11.SDA, Bauteil10.SDA, Bauteil9.SDA, Bauteil12.SDA
  N2: A1.Pin_14, Bauteil13.SCL, Bauteil11.SCL, Bauteil10.SCL, Bauteil9.SCL, Bauteil12.SCL
  N3: A1.Pin_33, Bauteil11.XSHUT
  N4: A1.Pin_34, Bauteil10.XSHUT
  N5: A1.Pin_35, Bauteil9.XSHUT
  N6: A1.Pin_36, Bauteil12.XSHUT
  N7: A1.Pin_37, Bauteil13.XSHUT

custom parts:
  Arduino R4 Minima: Introducing the Arduino UNO R4 Minima! This board boasts the RA4M1 microprocessor from Renesas, delivering increased processing power, expanded memory, and additional peripherals.
  GY-VL53L0XV2 Laser Ranger Module: The GY-VL53L0XV2 is based on the VL53L0X from ST Microelectronics, a time-of-flight ranging system integrated into a compact module.
